# Fritzing sketch rp2040wx_fritz (saved by Fritzing 1.0.0rc)
breadboards: 1

parts:
  Mod1 = Raspberry Pi Pico W
  Part1 = MPL3115A2 I2C Barometric Pressure, Altitude, Temperature Sensor
  Part2 = Adafruit DS3231 [part_number="Adafruit #3013"]
  Part3 = Adafruit SHT31-D Sensirion Temperature/Humidity Sensor [part_number="Adafruit #2857"]
  Part4 = I2C Non-Volatile FRAM 32KB

nets:
  GND: Mod1.pin_3, Mod1.pin_8, Mod1.pin_13, Mod1.pin_18, Mod1.pin_23, Mod1.pin_28, Mod1.pin_33, Mod1.pin_38, Part1.GND, Part2.GND, Part3.GND, Part4.GND
  N1: Mod1.pin_4, Part1.SDA, Part3.SDA
  N2: Mod1.pin_5, Part1.SCL, Part3.SCL
  N3: Mod1.pin_6, Part2.SDA, Part4.SDA
  N4: Mod1.pin_7, Part2.SCL, Part4.SCL
  N5: Mod1.pin_21, Part1.INT1
  N6: Mod1.pin_26, Part2.32KHZ
  N7: Mod1.pin_29, Part2.SQW
  VIN: Mod1.pin_37, Part1.VIN, Part2.Vin, Part3.VIN, Part4.VCC

custom parts:
  Raspberry Pi Pico W: Raspberry Pi Pico W. Based around the RP2040 microcontroller the Pico W is a low cost microcontroller device bringing Raspberry Pi quality, cost, and easy of use to the microcontroller space. The areas marked KEEPOUT in pcb silkscreen should not have traces running through them to avoid shorts on a soldered in module!
  MPL3115A2 I2C Barometric Pressure, Altitude, Temperature Sensor: This pressure sensor from Freescale is a great low-cost sensing solution for precision measurement of barometric pressure and altitude. The MPL3115A2 has a typical 1.5 Pascal resolution, which can resolve altitude at 0.3 meters (compare to the BMP180 which can do 0.17m). It has some upsides compared to the BMP180, such as interrupt outputs for ultra-low power usage, and its also a heck of a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
  Adafruit DS3231: The datasheet for the DS3231 explains that this part is an "Extremely Accurate I²C-Integrated RTC/TCXO/Crystal". And, hey, it does exactly what it says on the tin! This Real Time Clock (RTC) is the most precise you can get in a small, low power package. Most RTCs use an external 32kHz timing crystal that is used to keep time with low current draw. And that's all well and good, but those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
  Adafruit SHT31-D Sensirion Temperature/Humidity Sensor: Sensirion Temperature/Humidity sensors are some of the finest & highest-accuracy devices you can get. And, finally we have some that have a true I2C interface for easy reading. The SHT31-D sensor has an excellent ±2% relative humidity and ±0.3°C accuracy for most uses. Unlike earlier SHT sensors, this sensor has a true I2C interface, and (bonus!) even with two address options. It also is 3V or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
  I2C Non-Volatile FRAM 32KB: With our I2C FRAM breakout board you can add some FRAM storage to your next DIY project. FRAM allows for a lower power usage and a faster write performance. It's excellent for low-power or inconsistent-power datalogging or data buffering where you want to stream data fast while also keeping the data when there's no power. Unlike Flash or EEPROM there's no pages to worry about. Each byte can be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
